// Logisim project Final_version.circ as structural Verilog: 1 circuit, main circuit main
module main (
);

  wire buffer_1_out, button_1_out, button_2_out, button_3_out, button_4_out, button_5_out, button_6_out,
       button_7_out, button_8_out, button_9_out, cdm_8_mark5_1_data_inst, clk, Code, data, decoder_2_out0,
       decoder_2_out1, I_Osel, IAck, In_out_prime, IO_3_out, IRQ, mem, nand_1_out, not_1_out, not_2_out, RAM,
       \кнопочка_1_а_всё_уже , \кнопочка_1_если_первые_2_не_подошли , \кнопочка_1_победа ;
  wire [1:0] \сдр_1_h0 , \сдр_1_h1 , \сдр_1_h2 , \сдр_1_v0 , \сдр_1_v1 , \сдр_1_v2 ;
  wire [2:0] vec;
  wire [2:2] \тик_так_1_v1 , \тик_так_1_v2 , \тик_так_2_v1 , \тик_так_3_v1 , \тик_так_4_v2 , \тик_так_7_v2 ;
  wire [3:0] I_Oadr, \бпц_1_типа_координаты_х_и_у , \тик_так_1_r1 , \тик_так_1_r2 , \тик_так_1_r3 ,
       \тик_так_1_r4 , \тик_так_2_r1 , \тик_так_2_r2 , \тик_так_2_r3 , \тик_так_2_r4 , \тик_так_3_r1 ,
       \тик_так_3_r2 , \тик_так_3_r3 , \тик_так_3_r4 , \тик_так_4_r1 , \тик_так_4_r2 , \тик_так_4_r3 ,
       \тик_так_4_r4 , \тик_так_5_r1 , \тик_так_5_r2 , \тик_так_5_r3 , \тик_так_5_r4 , \тик_так_6_r1 ,
       \тик_так_6_r2 , \тик_так_6_r3 , \тик_так_6_r4 , \тик_так_7_r1 , \тик_так_7_r2 , \тик_так_7_r3 ,
       \тик_так_7_r4 , \тик_так_8_r1 , \тик_так_8_r2 , \тик_так_8_r3 , \тик_так_8_r4 , \тик_так_9_r1 ,
       \тик_так_9_r2 , \тик_так_9_r3 , \тик_так_9_r4 ;
  wire [7:0] cdm_8_mark5_1_data_out, cdm_8_mark5_1_pc, cdm_8_mark5_1_ps, cdm_8_mark5_1_r0, cdm_8_mark5_1_r1,
       cdm_8_mark5_1_r2, cdm_8_mark5_1_r3, cdm_8_mark5_1_sp, controlled_buffer_2_out, I_Odat;
  wire [7:4] cdm_8_mark5_1_addr;
  wire [7:7] \бпц_1_по_коням ;

  LED Runtime_error (.in(\кнопочка_1_если_первые_2_не_подошли ));
  LED Wrong_answer (.in(\кнопочка_1_а_всё_уже ));
  LED Accepted (.in(\кнопочка_1_победа ));
  \Кнопочка  \u_кнопочка_1  (
    .\Победа (\кнопочка_1_победа ), .\А_всё_уже (\кнопочка_1_а_всё_уже ), .\Счёт (I_Odat[7:6]),
    .\Если_первые_2_не_подошли (\кнопочка_1_если_первые_2_не_подошли ), .\Главная_штука (decoder_2_out0));
  \СДР  \u_сдр_1  (
    .symID(I_Odat[1:0]), .H0(\сдр_1_h0 ), .H1(\сдр_1_h1 ), .H2(\сдр_1_h2 ), .V0(\сдр_1_v0 ), .V1(\сдр_1_v1 ),
    .V2(\сдр_1_v2 ), .XY(I_Odat[5:2]), .\На_месте (decoder_2_out0));
  and and_1 (I_Osel, not_1_out, clk, data);
  // Probe on cdm_8_mark5_1_r0
  // Probe on cdm_8_mark5_1_r1
  not not_1 (not_1_out, nand_1_out);
  \Тик_Так  \u_тик_так_1  (
    .r1(\тик_так_1_r1 ), .r2(\тик_так_1_r2 ), .r3(\тик_так_1_r3 ), .r4(\тик_так_1_r4 ), ._1(\сдр_1_v0 ),
    ._2(\сдр_1_h0 ), .v2(\тик_так_1_v2 [2]), .v1(\тик_так_1_v1 [2]), .in_3(button_1_out));
  DotMatrix #(.inputtype("row"), .matrixcols(4), .matrixrows(4)) dotmatrix_1 (
    .row0(\тик_так_1_r1 ), .row1(\тик_так_1_r2 ), .row2(\тик_так_1_r3 ), .row3(\тик_так_1_r4 ));
  Button button_1 (.out(button_1_out));
  \Тик_Так  \u_тик_так_2  (
    .r1(\тик_так_2_r1 ), .r2(\тик_так_2_r2 ), .r3(\тик_так_2_r3 ), .r4(\тик_так_2_r4 ), ._1(\сдр_1_v0 ),
    ._2(\сдр_1_h1 ), .v2(\тик_так_1_v2 [2]), .v1(\тик_так_2_v1 [2]), .in_3(button_2_out));
  DotMatrix #(.inputtype("row"), .matrixcols(4), .matrixrows(4)) dotmatrix_2 (
    .row0(\тик_так_2_r1 ), .row1(\тик_так_2_r2 ), .row2(\тик_так_2_r3 ), .row3(\тик_так_2_r4 ));
  Button button_2 (.out(button_2_out));
  \Тик_Так  \u_тик_так_3  (
    .r1(\тик_так_3_r1 ), .r2(\тик_так_3_r2 ), .r3(\тик_так_3_r3 ), .r4(\тик_так_3_r4 ), ._1(\сдр_1_v0 ),
    ._2(\сдр_1_h2 ), .v2(\тик_так_1_v2 [2]), .v1(\тик_так_3_v1 [2]), .in_3(button_3_out));
  DotMatrix #(.inputtype("row"), .matrixcols(4), .matrixrows(4)) dotmatrix_3 (
    .row0(\тик_так_3_r1 ), .row1(\тик_так_3_r2 ), .row2(\тик_так_3_r3 ), .row3(\тик_так_3_r4 ));
  Button button_3 (.out(button_3_out));
  // Probe on cdm_8_mark5_1_r3
  // Probe on cdm_8_mark5_1_sp
  // Probe on cdm_8_mark5_1_pc
  // Probe on cdm_8_mark5_1_r2
  Clock clock_1 (.out(clk));
  nand nand_1 (nand_1_out, cdm_8_mark5_1_addr[4], cdm_8_mark5_1_addr[5], cdm_8_mark5_1_addr[6], cdm_8_mark5_1_addr[7]);
  and and_2 (RAM, nand_1_out, data);
  // Probe on cdm_8_mark5_1_ps
  CdM_8_mark5 cdm_8_mark5_1 (
    .clock(clk), .addr({cdm_8_mark5_1_addr, I_Oadr}), .mem_read(In_out_prime), .mem_cycle(mem),
    .data_inst(cdm_8_mark5_1_data_inst), .data_out(cdm_8_mark5_1_data_out),
    .data_in(controlled_buffer_2_out), .r0(cdm_8_mark5_1_r0), .r1(cdm_8_mark5_1_r1), .r2(cdm_8_mark5_1_r2),
    .r3(cdm_8_mark5_1_r3), .PC(cdm_8_mark5_1_pc), .SP(cdm_8_mark5_1_sp), .PS(cdm_8_mark5_1_ps), .IAck(IAck),
    .IRQ(IRQ), .vec(vec));
  \Тик_Так  \u_тик_так_4  (
    .r1(\тик_так_4_r1 ), .r2(\тик_так_4_r2 ), .r3(\тик_так_4_r3 ), .r4(\тик_так_4_r4 ), ._1(\сдр_1_v1 ),
    ._2(\сдр_1_h0 ), .v2(\тик_так_4_v2 [2]), .v1(\тик_так_1_v1 [2]), .in_3(button_4_out));
  DotMatrix #(.inputtype("row"), .matrixcols(4), .matrixrows(4)) dotmatrix_4 (
    .row0(\тик_так_4_r1 ), .row1(\тик_так_4_r2 ), .row2(\тик_так_4_r3 ), .row3(\тик_так_4_r4 ));
  Button button_4 (.out(button_4_out));
  \Тик_Так  \u_тик_так_5  (
    .r1(\тик_так_5_r1 ), .r2(\тик_так_5_r2 ), .r3(\тик_так_5_r3 ), .r4(\тик_так_5_r4 ), ._1(\сдр_1_v1 ),
    ._2(\сдр_1_h1 ), .v2(\тик_так_4_v2 [2]), .v1(\тик_так_2_v1 [2]), .in_3(button_5_out));
  DotMatrix #(.inputtype("row"), .matrixcols(4), .matrixrows(4)) dotmatrix_5 (
    .row0(\тик_так_5_r1 ), .row1(\тик_так_5_r2 ), .row2(\тик_так_5_r3 ), .row3(\тик_так_5_r4 ));
  Button button_5 (.out(button_5_out));
  \Тик_Так  \u_тик_так_6  (
    .r1(\тик_так_6_r1 ), .r2(\тик_так_6_r2 ), .r3(\тик_так_6_r3 ), .r4(\тик_так_6_r4 ), ._1(\сдр_1_v1 ),
    ._2(\сдр_1_h2 ), .v2(\тик_так_4_v2 [2]), .v1(\тик_так_3_v1 [2]), .in_3(button_6_out));
  DotMatrix #(.inputtype("row"), .matrixcols(4), .matrixrows(4)) dotmatrix_6 (
    .row0(\тик_так_6_r1 ), .row1(\тик_так_6_r2 ), .row2(\тик_так_6_r3 ), .row3(\тик_так_6_r4 ));
  Button button_6 (.out(button_6_out));
  buf buffer_1 (buffer_1_out, buffer_1_out);
  Decoder #(.disabled(0)) decoder_1 (.out0(Code), .out1(data), .sel(cdm_8_mark5_1_data_inst), .en(mem));
  assign I_Odat = not_2_out ? cdm_8_mark5_1_data_out : 8'bz;  // Controlled_Buffer controlled_buffer_1
  not not_2 (not_2_out, In_out_prime);
  assign controlled_buffer_2_out = In_out_prime ? I_Odat : 8'bz;  // Controlled_Buffer controlled_buffer_2
  and IO_3 (IO_3_out, I_Osel, I_Oadr[0], I_Oadr[1], ~I_Oadr[2], ~I_Oadr[3]);  // AND_Gate
  Decoder #(.disabled(0)) decoder_2 (.out0(decoder_2_out0), .out1(decoder_2_out1), .sel(In_out_prime), .en(IO_3_out));
  \Тик_Так  \u_тик_так_7  (
    .r1(\тик_так_7_r1 ), .r2(\тик_так_7_r2 ), .r3(\тик_так_7_r3 ), .r4(\тик_так_7_r4 ), ._1(\сдр_1_v2 ),
    ._2(\сдр_1_h0 ), .v2(\тик_так_7_v2 [2]), .v1(\тик_так_1_v1 [2]), .in_3(button_7_out));
  DotMatrix #(.inputtype("row"), .matrixcols(4), .matrixrows(4)) dotmatrix_7 (
    .row0(\тик_так_7_r1 ), .row1(\тик_так_7_r2 ), .row2(\тик_так_7_r3 ), .row3(\тик_так_7_r4 ));
  Button button_7 (.out(button_7_out));
  \Тик_Так  \u_тик_так_8  (
    .r1(\тик_так_8_r1 ), .r2(\тик_так_8_r2 ), .r3(\тик_так_8_r3 ), .r4(\тик_так_8_r4 ), ._1(\сдр_1_v2 ),
    ._2(\сдр_1_h1 ), .v2(\тик_так_7_v2 [2]), .v1(\тик_так_2_v1 [2]), .in_3(button_8_out));
  DotMatrix #(.inputtype("row"), .matrixcols(4), .matrixrows(4)) dotmatrix_8 (
    .row0(\тик_так_8_r1 ), .row1(\тик_так_8_r2 ), .row2(\тик_так_8_r3 ), .row3(\тик_так_8_r4 ));
  Button button_8 (.out(button_8_out));
  \Тик_Так  \u_тик_так_9  (
    .r1(\тик_так_9_r1 ), .r2(\тик_так_9_r2 ), .r3(\тик_так_9_r3 ), .r4(\тик_так_9_r4 ), ._1(\сдр_1_v2 ),
    ._2(\сдр_1_h2 ), .v2(\тик_так_7_v2 [2]), .v1(\тик_так_3_v1 [2]), .in_3(button_9_out));
  DotMatrix #(.inputtype("row"), .matrixcols(4), .matrixrows(4)) dotmatrix_9 (
    .row0(\тик_так_9_r1 ), .row1(\тик_так_9_r2 ), .row2(\тик_так_9_r3 ), .row3(\тик_так_9_r4 ));
  Button button_9 (.out(button_9_out));
  Pull_Resistor pull_resistor_1 (.node(I_Oadr[0]));
  Pull_Resistor pull_resistor_2 (.node(I_Oadr[1]));
  Pull_Resistor pull_resistor_3 (.node(I_Oadr[2]));
  Pull_Resistor pull_resistor_4 (.node(I_Oadr[3]));
  Pull_Resistor pull_resistor_5 (.node(cdm_8_mark5_1_addr[4]));
  Pull_Resistor pull_resistor_6 (.node(cdm_8_mark5_1_addr[5]));
  Pull_Resistor pull_resistor_7 (.node(cdm_8_mark5_1_addr[6]));
  Pull_Resistor pull_resistor_8 (.node(cdm_8_mark5_1_addr[7]));
  ROM rom_1 (.addr({cdm_8_mark5_1_addr, I_Oadr}), .data(I_Odat), .sel(Code));
  RAM ram_1 (.addr({cdm_8_mark5_1_addr, I_Oadr}), .data(I_Odat), .sel(RAM), .clk(clk), .ld(In_out_prime));  // open: clr
  assign I_Odat = decoder_2_out1 ? {\бпц_1_по_коням [7], 3'b000, \бпц_1_типа_координаты_х_и_у } : 8'bz;  // Controlled_Buffer controlled_buffer_3
  \БПЦ  \u_бпц_1  (
    .V0(\тик_так_1_v2 [2]), .V1(\тик_так_4_v2 [2]), .V2(\тик_так_7_v2 [2]), .\На_месте (decoder_2_out1),
    .H0(\тик_так_1_v1 [2]), .H1(\тик_так_2_v1 [2]), .H2(\тик_так_3_v1 [2]), .\По_коням (\бпц_1_по_коням [7]),
    .\Типа_координаты_Х_и_У (\бпц_1_типа_координаты_х_и_у ));

  // Other names for the same wires on the sheet: rd_wr_prime = In_out_prime

  // Notes on the sheet:
  //   buffer_1 drives only 1 and floats otherwise
  //   contents of rom_1 (hex, n*v repeats v):
  //   1 2 3 5 6 7 9 a b 1 5 9 2 6 a 3 7 b 1 6 b 3 6 9 d0 0 d1 18 f2 a2 8c 89 e1 1c d0 f3 b1 5 e4 2a ee 24
  //   d2 7f 49 8d d2 18 d0 0 b3 7d e1 39 d3 0 a3 8c 8a e1 32 89 95 95 8d 8d d0 f3 a1 d2 8 d0 0 b1 8c b3 8c
  //   17 b1 17 e1 58 d0 f3 d1 7f a1 d4 8c 8a e1 49 d0 0 d2 9 d3 0 b1 17 8c 8a e1 62 f e5 71 d0 f3 d1 ff a1
  //   d4 d0 0 d2 4 18 b2 e1 82 d0 0 b2 ed 82 d3 1 ee cc a ed 89 d3 6 ee cc d0 0 d2 8 b1 8c b3 77 e1 9b 8c
  //   b3 f ed 9b ee cc 88 8c b3 77 e1 a8 88 b3 f ed a7 ee cc 8c 88 b1 77 e1 b5 88 b3 f ed b4 ee cc 8c 8c
  //   8c 8a e1 8d d2 0 d1 ff a e1 cc b3 7b e0 c9 77 e0 c9 8e 8c ee be d0 0 d2 18 b1 7d e1 d7 d1 ff a1 8c
  //   8a e1 d0 8b 97 97 8f d0 f3 a3 d2 8 d0 0 b1 8c b3 8c 17 b1 17 d1 fd 7d e1 f8 d0 f3 d1 bf a1 d4 8c 8a
  //   e1 e6 ee 22
endmodule
