// Logisim project project_chip.circ as structural Verilog: 5 circuits, main circuit Тик Так
module \Тик_Так  (
  input  [1:0] _1,
  input  [1:0] _2,
  input  in_3,
  output [3:0] r1,
  output [3:0] r2,
  output [3:0] r3,
  output [3:0] r4,
  output v2,
  output v1
);

  wire and_1_out, and_2_out, controlled_buffer_2_out, nor_1_out;
  wire [1:0] controlled_buffer_1_out;
  wire [15:0] multiplexer_2_out, register_1_q;

  Transistor #(.\type ("n")) transistor_1 (.in(controlled_buffer_2_out), .out(v1), .gate(controlled_buffer_2_out));
  and and_1 (and_1_out, _1[1], _2[1]);
  assign controlled_buffer_1_out = and_1_out ? {_2[0], _1[0]} : 2'bz;  // Controlled_Buffer controlled_buffer_1
  // Probe on {r4, r3, r2, r1}
  // Probe on controlled_buffer_1_out
  Multiplexer #(.width(16), .enable("false")) multiplexer_1 (
    .in0(register_1_q), .in1(16'h6909), .out({r4, r3, r2, r1}), .sel(and_2_out));
  and and_2 (and_2_out, ~nor_1_out, in_3);  // AND_Gate
  nor nor_1 (nor_1_out, r1[3], r1[2], r1[1], r1[0]);
  assign controlled_buffer_2_out = nor_1_out ? in_3 : 1'bz;  // Controlled_Buffer controlled_buffer_2
  // Probe on multiplexer_2_out
  Register #(.width(16), .trigger("high")) register_1 (
    .D(multiplexer_2_out), .Q(register_1_q), .clk(and_1_out));  // open: en, clr
  Multiplexer #(.select(2), .width(16), .enable("false")) multiplexer_2 (
    .in0({16{1'b0}}), .in1(16'h9429), .in2(16'hf99f), .out(multiplexer_2_out), .sel(controlled_buffer_1_out));  // open: in3

  assign v2 = v1;
endmodule

module \Кнопочка  (
  input  [1:0] \Счёт ,
  input  \Главная_штука ,
  output \Победа ,
  output \А_всё_уже ,
  output \Если_первые_2_не_подошли 
);

  wire [1:0] register_1_q;

  Pull_Resistor pull_resistor_1 (.node(\Победа ));
  Pull_Resistor pull_resistor_2 (.node(\А_всё_уже ));
  Pull_Resistor pull_resistor_3 (.node(\Если_первые_2_не_подошли ));
  Decoder #(.select(2), .enable("false")) decoder_1 (
    .out1(\Победа ), .out2(\А_всё_уже ), .out3(\Если_первые_2_не_подошли ), .sel(register_1_q));  // open: out0
  Register #(.width(2), .trigger("high")) register_1 (
    .D(\Счёт ), .en(\Главная_штука ), .Q(register_1_q), .clk(\Главная_штука ));  // open: clr
  Pull_Resistor pull_resistor_4 (.node(\Главная_штука ));
endmodule

module \СДР  (
  input  [3:0] XY,
  input  [1:0] symID,
  input  \На_месте ,
  output [1:0] H0,
  output [1:0] H1,
  output [1:0] H2,
  output [1:0] V0,
  output [1:0] V1,
  output [1:0] V2
);

  wire [3:0] bitselector_1_out;

  BitSelector #(.group(4)) bitselector_1 (.in({XY, 4'b1111}), .out(bitselector_1_out), .sel(\На_месте ));
  BitSelector #(.width(9), .group(3)) bitselector_2 (
    .in(9'h111), .out({H2[1], H1[1], H0[1]}), .sel(bitselector_1_out[3:2]));
  BitSelector #(.width(9), .group(3)) bitselector_3 (
    .in(9'h111), .out({V2[1], V1[1], V0[1]}), .sel(bitselector_1_out[1:0]));
  Pull_Resistor pull_resistor_1 (.node(H0[1]));
  Pull_Resistor pull_resistor_2 (.node(H1[1]));
  Pull_Resistor pull_resistor_3 (.node(H2[1]));
  Pull_Resistor pull_resistor_4 (.node(V0[1]));
  Pull_Resistor pull_resistor_5 (.node(V1[1]));
  Pull_Resistor pull_resistor_6 (.node(V2[1]));

  assign H0[0] = symID[0];
  assign H1[0] = symID[0];
  assign H2[0] = symID[0];
  assign V0[0] = symID[1];
  assign V1[0] = symID[1];
  assign V2[0] = symID[1];
endmodule

module \БПЦ  (
  input  V0,
  input  V1,
  input  V2,
  input  \На_месте ,
  input  H0,
  input  H1,
  input  H2,
  output \По_коням ,
  output [3:0] \Типа_координаты_Х_и_У 
);

  wire or_1_out, or_2_out;
  wire [1:0] \давай_всё_усложним_1_exit , \давай_всё_усложним_2_exit ;

  Pull_Resistor pull_resistor_1 (.node(V0));
  Pull_Resistor pull_resistor_2 (.node(V1));
  Pull_Resistor pull_resistor_3 (.node(V2));
  Pull_Resistor pull_resistor_4 (.node(H0));
  Pull_Resistor pull_resistor_5 (.node(H1));
  Pull_Resistor pull_resistor_6 (.node(H2));
  or or_1 (or_1_out, V0, V1, V2);
  or or_2 (or_2_out, H0, H1, H2);
  \Давай_всё_усложним  \u_давай_всё_усложним_1  (._0(V0), ._1(V1), ._2(V2), .exit(\давай_всё_усложним_1_exit ));
  and and_1 (\По_коням , or_1_out, \На_месте , or_2_out);
  \Давай_всё_усложним  \u_давай_всё_усложним_2  (._0(H0), ._1(H1), ._2(H2), .exit(\давай_всё_усложним_2_exit ));
  assign \Типа_координаты_Х_и_У  = \На_месте  ? {\давай_всё_усложним_2_exit , \давай_всё_усложним_1_exit } : 4'bz;  // Controlled_Buffer controlled_buffer_1
  Pull_Resistor pull_resistor_7 (.node(\Типа_координаты_Х_и_У ));

  // Notes on the sheet:
  //   Y
  //   X
  //   Y
  //   X
endmodule

module \Давай_всё_усложним  (
  input  _0,
  input  _1,
  input  _2,
  output [1:0] exit
);

  wire not_1_out;

  not not_1 (not_1_out, _0);
  BitSelector #(.width(4), .group(2)) bitselector_1 (.in({_2, _1, 2'b00}), .out(exit), .sel(not_1_out));
endmodule
